# Fritzing sketch pca9685_connection (saved by Fritzing 0.9.3b)

parts:
  パーツ1 = 16-Channel 12-bit PCA9685 PWM/Servo Driver
  J1 = Basic Servo
  Power_plug3 = Power plug
  パーツ3 = Arduino Uno (Rev3)
  J2 = Basic Servo
  J3 = Basic Servo
  J4 = Basic Servo
  J5 = Basic Servo
  J6 = Basic Servo
  J8 = Basic Servo
  J9 = Basic Servo
  J10 = Basic Servo
  J11 = Basic Servo
  J12 = Basic Servo
  J13 = Basic Servo

nets:
  N1: パーツ1.0, J1.pulse
  VCC: パーツ1.V+, J1.vcc, Power_plug3.VCC, J2.vcc, J3.vcc, J4.vcc, J5.vcc, J6.vcc, J8.vcc, J9.vcc, J10.vcc, J11.vcc, J12.vcc, J13.vcc
  GND: パーツ1.GND, パーツ3.pin_9, J2.gnd, J3.gnd, J4.gnd, J5.gnd, J6.gnd, J8.gnd, J9.gnd, J10.gnd, J11.gnd, J12.gnd, J13.gnd
  N2: パーツ1.1, J2.pulse
  N3: パーツ1.2, J3.pulse
  N4: パーツ1.3, J4.pulse
  N5: パーツ1.4, J5.pulse
  N6: パーツ1.5, J6.pulse
  N7: パーツ1.6, J8.pulse
  N8: パーツ1.7, J9.pulse
  N9: パーツ1.VCC, パーツ3.pin_1
  N10: パーツ1.SDA, パーツ3.pin_3
  N11: パーツ1.SCL, パーツ3.pin_5
  N12: パーツ1.8, J10.pulse
  N13: パーツ1.9, J11.pulse
  N14: パーツ1.10, J12.pulse
  N15: パーツ1.11, J13.pulse
  N16: Power_plug3.GND, パーツ3.pin_39

custom parts:
  16-Channel 12-bit PCA9685 PWM/Servo Driver: The Adafruit 16-Channel 12-bit PWM/Servo Driver will drive up to 16 servos over I2C with only 2 pins. The on-board PCA9685 PWM controller will drive all 16 channels simultaneously with no additional processing overhead. What's more, you can chain up to 62 of them to control up to 992 servos - all with the same 2 pins
  Power plug: power plug
  Arduino Uno (Rev3): The Arduino Uno is a microcontroller board based on the ATmega328 (datasheet). It has 14 digital input/output pins (of which 6 can be used as PWM outputs), 6 analog inputs, a 16 MHz ceramic resonator, a USB connection, a power jack, an ICSP header, and a reset button. It contains everything needed to support the microcontroller; simply connect it to a computer with a USB cable or power it with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
